# Fritzing sketch Schematic (saved by Fritzing 0.9.3b)
circuit board: 14.9152cm x 11.3347cm
breadboards: 1

parts:
  hc-sr1 = hc-sr04
  RTC_DS3231 = ZS-042 RTC Module
  Relay = 2-Channel 5v Relay Shield [package=relay-2ch5v10a]
  LED1 = LEDs [package=led10mm]
  Fan = Fan - Ventilador [package=THT]
  NodeMCU = NodeMCU V3.0
  SERVO1 = Tower Pro SG90 servo [part_number=101246]
  J1 = Piezo Speaker
  Mod1 = KY-015 Temperature & Humidity Sensor Module [package="Breakout board"]
  R1 = Resistor [tolerance=±5% resistance=220 package="2512 [SMD]"]

nets:
  VCC: hc-sr1.VCC, RTC_DS3231.VCC, NodeMCU.3V3, SERVO1.+5V, J1.pin2, Mod1.+
  N1: hc-sr1.Trig, NodeMCU.D6
  N2: hc-sr1.Echo, NodeMCU.D7
  GND: hc-sr1.GND, RTC_DS3231.GND, Relay.GND, Relay.K1-Off, Relay.K2-Off, Fan.GND, NodeMCU.GND, SERVO1.GND, Mod1.-, R1.Pin_1
  N3: RTC_DS3231.SDA, NodeMCU.D1
  N4: RTC_DS3231.SCL, NodeMCU.D2
  VCC_2: Relay.VCC, Relay.K1-On, Relay.K2-On, NodeMCU.Vin
  N5: Relay.IN1, NodeMCU.D3
  N6: Relay.IN2, NodeMCU.D4
  N7: Relay.K1-In, Fan.5V
  N8: Relay.K2-In, LED1.A
  N9: LED1.C, R1.Pin_0
  N10: NodeMCU.D5, SERVO1.Signal
  N11: NodeMCU.D8, J1.pin1
  N12: NodeMCU.RX, Mod1.Data

custom parts:
  2-Channel 5v Relay Shield: 2 Channel 5v Relay Shield w. 2x SPD-06VDC-SD-C
  Fan - Ventilador: Ventilador de 2 pines, se encuentra comunmente en computadoras de escritorio
  NodeMCU V3.0: ESP8266 based NodeMCU
  Tower Pro SG90 servo: Original file by John De Cristofaro http://www.adafruit.com/products/1449 Adafruit Feedback Servo (Small) Edited by: e-radionica.com 28/9/2015
  KY-015 Temperature & Humidity Sensor Module: KY-015 temperature and humidity sensor module, provides a low-latency serial interface to measure humidity and temperature.
