# Fritzing sketch Schematic_PCB (saved by Fritzing 0.9.3b)
circuit board: 14.9152cm x 11.3347cm
breadboards: 1

parts:
  hc-sr1 = hc-sr04
  RTC_DS3231 = ZS-042 RTC Module
  Servo = Basic Servo
  Relay = 2-Channel 5v Relay Shield [package=relay-2ch5v10a]
  LED1 = LEDs [package=led10mm]
  Fan = Fan - Ventilador [package=THT]
  NodeMCU = NodeMCU V3.0
  Mod1 = KY-015 Temperature & Humidity Sensor Module [package="Breakout board"]

nets:
  VCC: hc-sr1.VCC, RTC_DS3231.VCC, Servo.vcc, NodeMCU.3V3, Mod1.S
  N1: hc-sr1.Trig, NodeMCU.D6
  N2: hc-sr1.Echo, NodeMCU.D7
  GND: hc-sr1.GND, RTC_DS3231.GND, Relay.GND, Relay.K1-Off, Relay.K2-Off, LED1.C, Fan.GND, NodeMCU.GND, Mod1.-
  N3: RTC_DS3231.SDA, NodeMCU.D1
  N4: RTC_DS3231.SCL, NodeMCU.D2
  N5: Servo.pulse, NodeMCU.D5
  VCC_2: Relay.VCC, Relay.K1-On, Relay.K2-On, NodeMCU.Vin
  N6: Relay.IN1, NodeMCU.D3
  N7: Relay.IN2, NodeMCU.D4
  N8: Relay.K1-In, Fan.5V
  N9: Relay.K2-In, LED1.A
  N10: NodeMCU.RX, Mod1.Vin

custom parts:
  2-Channel 5v Relay Shield: 2 Channel 5v Relay Shield w. 2x SPD-06VDC-SD-C
  Fan - Ventilador: Ventilador de 2 pines, se encuentra comunmente en computadoras de escritorio
  NodeMCU V3.0: ESP8266 based NodeMCU
  KY-015 Temperature & Humidity Sensor Module: KY-015 temperature and humidity sensor module, provides a low-latency serial interface to measure humidity and temperature.
